// Logisim project Exemple de ROM à transistors 4 mots.circ as structural Verilog: 1 circuit, main circuit main
// 0x3
module main (
  input  Lecture,
  input  [1:0] adresse
);

  wire decoder_1_out0, decoder_1_out1, decoder_1_out2, decoder_1_out3, pull_resistor_1_node,
       pull_resistor_2_node, pull_resistor_3_node, transistor_3_out;

  Decoder #(.select(2), .disabled(0)) decoder_1 (
    .out0(decoder_1_out0), .out1(decoder_1_out1), .out2(decoder_1_out2), .out3(decoder_1_out3),
    .sel(adresse), .en(1'b1));
  Pull_Resistor pull_resistor_1 (.node(pull_resistor_1_node));
  Transistor #(.\type ("n")) transistor_1 (.in(Lecture), .out(pull_resistor_1_node), .gate(decoder_1_out0));
  LED led_1 (.in(pull_resistor_1_node));
  Pull_Resistor pull_resistor_2 (.node(pull_resistor_2_node));
  Transistor #(.\type ("n")) transistor_2 (.in(Lecture), .out(pull_resistor_2_node), .gate(decoder_1_out1));
  Transistor #(.\type ("n")) transistor_3 (.in(Lecture), .out(transistor_3_out), .gate(decoder_1_out2));
  LED led_2 (.in(pull_resistor_2_node));
  Pull_Resistor pull_resistor_3 (.node(pull_resistor_3_node));
  Pull_Resistor pull_resistor_4 (.node(transistor_3_out));
  Transistor #(.\type ("n")) transistor_4 (.in(Lecture), .out(pull_resistor_3_node), .gate(decoder_1_out3));
  LED led_3 (.in(pull_resistor_3_node));
  LED led_4 (.in(transistor_3_out));
  ROM rom_1 ();  // open: addr, data, sel
  RAM ram_1 ();  // open: addr, data, sel, clk, ld, clr
  LED led_5 ();  // open: in

  // Notes on the sheet:
  //   Validation
  //   contents of rom_1 (hex, n*v repeats v):
  //   4*11
endmodule
